# Fritzing sketch nano-nrf24-1 (saved by Fritzing 0.9.4)
breadboards: 1

parts:
  Part1 = Arduino Nano (Rev3.0)
  Part3 = NRF24L01+ Breakout Board
  RHT2 = Humidity and Temperature Sensor RHT03
  R5 = Resistor [tolerance=±5% resistance=10k package=THT]

nets:
  GND: Part1.GND, Part3.GND, RHT2.GND_2
  N1: Part1.D2, R5.Pin_0
  N2: Part1.D9, Part3.CS
  N3: Part1.D10, Part3.CE
  N4: Part1.D11/MOSI, Part3.MOSI
  N5: Part1.D12/MISO, Part3.MISO
  VCC: Part1.3V3, Part3.VCC, RHT2.Vcc
  N6: Part1.D13/SCK, Part3.SCK
  N7: RHT2.Data-signal, R5.Pin_1
