# Fritzing sketch pizw-nrf24-2 (saved by Fritzing 0.9.4)
breadboards: 1

parts:
  MCU1 = Raspberry Pi Zero
  Part2 = NRF24L01+ Breakout Board
  Part3 = NRF24L01+ Breakout Board

nets:
  VCC: MCU1.pin_1, MCU1.pin_17, Part2.VCC, Part3.VCC
  GND: MCU1.pin_6, MCU1.pin_30, Part2.GND, Part3.GND
  N1: MCU1.pin_19, Part2.MOSI
  N2: MCU1.pin_21, Part2.MISO
  N3: MCU1.pin_22, Part2.CE
  N4: MCU1.pin_23, Part2.SCK
  N5: MCU1.pin_24, Part2.CS
  N6: MCU1.pin_32, Part3.CE
  N7: MCU1.pin_35, Part3.MISO
  N8: MCU1.pin_36, Part3.CS
  N9: MCU1.pin_38, Part3.MOSI
  N10: MCU1.pin_40, Part3.SCK
